# Fritzing sketch kangmin-roughsketch (saved by Fritzing 0.9.3b)
breadboards: 1

parts:
  부품1 = Arduino Uno (Rev3) - ICSP
  SP1 = SPEAKER [package=pcb_mount_speaker]
  S1 = Pushbutton [package="[SMD]"]
  S2 = Momentary Switch [package=ksa_sealed_tac_switch]
  DFRobot_DFPlayer_Mini1 = DFRobot DFPlayer Mini [part_number=DFR0299]

nets:
  N1: 부품1.GND, SP1.+, DFRobot_DFPlayer_Mini1.GND-1, DFRobot_DFPlayer_Mini1.GND-2
  3V3: 부품1.3V3, S1.Pin_3, S1.Pin_4, S2.4, DFRobot_DFPlayer_Mini1.VCC, DFRobot_DFPlayer_Mini1.IO_1
  N2: SP1.-, DFRobot_DFPlayer_Mini1.SPK_1, DFRobot_DFPlayer_Mini1.SPK_2
  N3: S1.Pin_1, S1.Pin_2
  N4: S2.3, DFRobot_DFPlayer_Mini1.IO_2

notes:
  Short press to play previous, long press to decrease volume
  Short press to play next, long press to increase volume
