# Fritzing sketch jongchae-roughsketch (saved by Fritzing 0.9.3b)
breadboards: 1

parts:
  부품1 = Arduino Uno (Rev3) - ICSP
  LED1 = smd LED [color="Red (633nm)" package="0603 [SMD]"]
  LED2 = smd LED [color="Red (633nm)" package="0603 [SMD]"]
  LED3 = smd LED [color="Red (633nm)" package="0603 [SMD]"]
  LED4 = smd LED [color="Red (633nm)" package="0603 [SMD]"]
  LED5 = smd LED [color="Red (633nm)" package="0603 [SMD]"]
  LED6 = smd LED [color="Red (633nm)" package="0603 [SMD]"]
  R1 = Resistor [tolerance=±5% resistance=220 package=THT]
  R2 = Resistor [tolerance=±5% resistance=220 package=THT]
  R3 = Resistor [tolerance=±5% resistance=220 package=THT]
  M1 = DC Motor
  Q1 = NPN-Transistor [package="TO92 [THT]"]
  D1 = Zener Diode [part_number=1N4732A breakdown_voltage=3.6V package="Melf DO-213 AB [SMD]"]
  R4 = Resistor [tolerance=±5% resistance=220 package=THT]

nets:
  N1: 부품1.D8, R3.Pin_1
  N2: 부품1.D9_PWM, R2.Pin_1
  N3: 부품1.D10_PWM/SS, R1.Pin_1
  N4: 부품1.D2, R4.Pin_0
  N5: 부품1.5V, M1.pin_1, D1.cathode
  N6: 부품1.GND, LED1.cathode, LED2.cathode, LED3.cathode, LED4.cathode, LED5.cathode, LED6.cathode, Q1.E
  N7: LED1.anode, LED2.anode, R1.Pin_0
  N8: LED3.anode, LED4.anode, R3.Pin_0
  N9: LED5.anode, LED6.anode, R2.Pin_0
  N10: M1.pin_2, Q1.C, D1.anode
  N11: Q1.B, R4.Pin_1
