# Fritzing sketch jongchae-sketch (saved by Fritzing 0.9.3b)
breadboards: 1

parts:
  부품1 = Arduino Uno (Rev3) - ICSP
  LED1 = smd LED [color="Red (633nm)" package="0603 [SMD]"]
  LED2 = smd LED [color="Red (633nm)" package="0603 [SMD]"]
  LED3 = smd LED [color="Red (633nm)" package="0603 [SMD]"]
  LED4 = smd LED [color="Red (633nm)" package="0603 [SMD]"]
  LED5 = smd LED [color="Red (633nm)" package="0603 [SMD]"]
  LED6 = smd LED [color="Red (633nm)" package="0603 [SMD]"]
  R1 = Resistor [tolerance=±5% resistance=100 package=THT]
  R2 = Resistor [tolerance=±5% resistance=100 package=THT]
  R3 = Resistor [tolerance=±5% resistance=100 package=THT]
  J1 = Basic Servo
  LED7 = smd LED [color="Red (633nm)" package="0603 [SMD]"]
  LED8 = smd LED [color="Red (633nm)" package="0603 [SMD]"]
  R4 = Resistor [tolerance=±5% resistance=100 package=THT]

nets:
  N1: 부품1.ICSP_MOSI, 부품1.D11_PWM/MOSI, R1.Pin_1
  N2: 부품1.D8, R4.Pin_1
  N3: 부품1.D9_PWM, R3.Pin_1
  N4: 부품1.D10_PWM/SS, R2.Pin_1
  GND: 부품1.GND, LED1.cathode, LED2.cathode, LED3.cathode, LED4.cathode, LED5.cathode, LED6.cathode, J1.gnd, LED7.cathode, LED8.cathode
  N5: 부품1.D3_PWM, J1.pulse
  5V: 부품1.5V, J1.vcc
  N6: LED1.anode, LED2.anode, R1.Pin_0
  N7: LED3.anode, LED4.anode, R3.Pin_0
  N8: LED5.anode, LED6.anode, R2.Pin_0
  N9: LED7.anode, LED8.anode, R4.Pin_0
