# Fritzing sketch jooheon-roughsketch (saved by Fritzing 0.9.3b)
breadboards: 1

parts:
  부품1 = Arduino Uno (Rev3) - ICSP
  M3 = DC Motor
  M4 = DC Motor
  Q1 = NPN-Transistor [package="TO92 [THT]"]
  D1 = Zener Diode [part_number=1N4732A breakdown_voltage=3.6V package="Melf DO-213 AB [SMD]"]
  R1 = Resistor [tolerance=±5% resistance=220 package="2010 [SMD]"]
  J1 = Piezo Speaker
  LED1 = smd LED [color="Red (633nm)" package="1206 [SMD]"]
  R2 = Resistor [tolerance=±5% resistance=220 package="2010 [SMD]"]
  LED2 = LEDs [package=led10mm]
  R3 = Resistor [tolerance=±5% resistance=220 package="2010 [SMD]"]

nets:
  N1: 부품1.D8, R3.Pin_1
  N2: 부품1.D10_PWM/SS, R2.Pin_1
  N3: 부품1.D2, R1.Pin_0
  N4: 부품1.D3_PWM, J1.pin2
  N5: 부품1.5V, M3.pin_1, M4.pin_1, D1.cathode
  N6: 부품1.GND, Q1.E, J1.pin1, LED1.cathode, LED2.C
  N7: M3.pin_2, M4.pin_2, Q1.C, D1.anode
  N8: Q1.B, R1.Pin_1
  N9: LED1.anode, R2.Pin_0
  N10: LED2.A, R3.Pin_0
