# Fritzing sketch jooheon-sketch (saved by Fritzing 0.9.3b)
breadboards: 1

parts:
  부품1 = Arduino Uno (Rev3) - ICSP
  M3 = DC Motor
  J1 = Piezo Speaker
  LED1 = smd LED [color="Red (633nm)" package="1206 [SMD]"]
  R2 = Resistor [tolerance=±5% resistance=10k package="2010 [SMD]"]
  LED2 = LEDs [package=led10mm]
  R3 = Resistor [tolerance=±5% resistance=10k package="2010 [SMD]"]
  M4 = DC Motor
  S1 = H-Bridge with L298N

nets:
  N1: 부품1.D8, J1.pin2
  N2: 부품1.D9_PWM, R3.Pin_1
  N3: 부품1.D10_PWM/SS, R2.Pin_1
  N4: 부품1.D5_PWM, S1.IN1, S1.IN3
  N5: 부품1.D6_PWM, S1.IN2, S1.IN4
  5V: 부품1.5V, S1.5V
  GND: 부품1.GND, J1.pin1, LED1.cathode, LED2.C, S1.GND
  N6: M3.pin_1, S1.M2-02
  N7: M3.pin_2, S1.M2-01
  N8: LED1.anode, R2.Pin_0
  N9: LED2.A, R3.Pin_0
  N10: M4.pin_1, S1.M1-02
  N11: M4.pin_2, S1.M1-01

custom parts:
  H-Bridge with L298N: h-bridge
