# Fritzing sketch namyoon-roughsketch (saved by Fritzing 0.9.3b)
breadboards: 1

parts:
  M5 = DC Motor
  Q2 = NPN-Transistor [package="TO92 [THT]"]
  D2 = Zener Diode [part_number=1N4732A breakdown_voltage=3.6V package="Melf DO-213 AB [SMD]"]
  R4 = Resistor [tolerance=±5% resistance=220 package="2010 [SMD]"]
  R5 = Resistor [tolerance=±5% resistance=220 package="2010 [SMD]"]
  LED3 = smd LED [color="Red (633nm)" package="1206 [SMD]"]
  J2 = Piezo Speaker
  부품3 = Arduino Mega ADK (Rev3)
  S1 = Pushbutton [package="[THT]"]
  S2 = Pushbutton [package="[SMD]"]
  S3 = Pushbutton [package="[SMD]"]
  S4 = Pushbutton [package="[SMD]"]
  S5 = Pushbutton [package="[SMD]"]
  S6 = Pushbutton [package="[SMD]"]
  S7 = Pushbutton [package="[SMD]"]
  S8 = Pushbutton [package="[SMD]"]
  S9 = Pushbutton [package="[SMD]"]
  S10 = Pushbutton [package="[SMD]"]
  S11 = Pushbutton [package="[SMD]"]
  S12 = Pushbutton [package="[SMD]"]

nets:
  N1: M5.pin_1, D2.cathode, 부품3.5V
  N2: M5.pin_2, Q2.C, D2.anode
  N3: Q2.E, LED3.cathode, J2.pin1, 부품3.GND
  N4: Q2.B, R4.Pin_1
  N5: R4.Pin_0, 부품3.D2_PWM
  N6: R5.Pin_0, LED3.anode
  N7: R5.Pin_1, 부품3.D8_PWM
  N8: J2.pin2, 부품3.D3_PWM
  N9: 부품3.3V3, 부품3.D22, 부품3.D24, 부품3.D26, 부품3.D28, 부품3.D30, 부품3.D32, 부품3.D34, 부품3.D36, 부품3.D38, 부품3.D40, 부품3.D42, 부품3.D44, S1.Pin_3, S1.Pin_4, S2.Pin_3, S2.Pin_4, S3.Pin_3, S3.Pin_4, S4.Pin_3, S4.Pin_4, S5.Pin_3, S5.Pin_4, S6.Pin_3, S6.Pin_4, S7.Pin_3, S7.Pin_4, S8.Pin_3, S8.Pin_4, S9.Pin_3, S9.Pin_4, S10.Pin_3, S10.Pin_4, S11.Pin_3, S11.Pin_4, S12.Pin_3, S12.Pin_4
  N10: S1.Pin_1, S1.Pin_2
  N11: S2.Pin_1, S2.Pin_2
  N12: S3.Pin_1, S3.Pin_2
  N13: S4.Pin_1, S4.Pin_2
  N14: S5.Pin_1, S5.Pin_2
  N15: S6.Pin_1, S6.Pin_2
  N16: S7.Pin_1, S7.Pin_2
  N17: S8.Pin_1, S8.Pin_2
  N18: S9.Pin_1, S9.Pin_2
  N19: S10.Pin_1, S10.Pin_2
  N20: S11.Pin_1, S11.Pin_2
  N21: S12.Pin_1, S12.Pin_2
