# Fritzing sketch namyoon-sketch (saved by Fritzing 0.9.3b)
breadboards: 1

parts:
  R5 = Resistor [tolerance=±5% resistance=220 package="2010 [SMD]"]
  LED3 = smd LED [color="Red (633nm)" package="1206 [SMD]"]
  J2 = Piezo Speaker
  부품3 = Arduino Mega ADK (Rev3)
  S1 = Pushbutton [package="[THT]"]
  S2 = Pushbutton [package="[SMD]"]
  S3 = Pushbutton [package="[SMD]"]
  S4 = Pushbutton [package="[SMD]"]
  S5 = Pushbutton [package="[SMD]"]
  S6 = Pushbutton [package="[SMD]"]
  S7 = Pushbutton [package="[SMD]"]
  S8 = Pushbutton [package="[SMD]"]
  S9 = Pushbutton [package="[SMD]"]
  S10 = Pushbutton [package="[SMD]"]
  S12 = Pushbutton [package="[SMD]"]
  R6 = Resistor [tolerance=±5% resistance=10k package=THT]
  R7 = Resistor [tolerance=±5% resistance=10k package=THT]
  R8 = Resistor [tolerance=±5% resistance=10k package=THT]
  R9 = Resistor [tolerance=±5% resistance=10k package=THT]
  R10 = Resistor [tolerance=±5% resistance=10k package=THT]
  R11 = Resistor [tolerance=±5% resistance=10k package=THT]
  R12 = Resistor [tolerance=±5% resistance=10k package=THT]
  R13 = Resistor [tolerance=±5% resistance=10k package=THT]
  R14 = Resistor [tolerance=±5% resistance=10k package=THT]
  R15 = Resistor [tolerance=±5% resistance=10k package=THT]
  R17 = Resistor [tolerance=±5% resistance=10k package=THT]
  J3 = Basic Servo

nets:
  N1: R5.Pin_0, LED3.anode
  N2: R5.Pin_1, 부품3.D6_PWM
  GND: LED3.cathode, J2.pin1, 부품3.GND, R6.Pin_1, R7.Pin_1, R8.Pin_1, R9.Pin_1, R10.Pin_1, R11.Pin_1, R12.Pin_1, R13.Pin_1, R14.Pin_1, R15.Pin_1, R17.Pin_1, J3.gnd
  N3: J2.pin2, 부품3.D7_PWM
  3V3: 부품3.3V3, S1.Pin_3, S1.Pin_4, S2.Pin_3, S2.Pin_4, S3.Pin_3, S3.Pin_4, S4.Pin_3, S4.Pin_4, S5.Pin_3, S5.Pin_4, S6.Pin_3, S6.Pin_4, S7.Pin_3, S7.Pin_4, S8.Pin_3, S8.Pin_4, S9.Pin_3, S9.Pin_4, S10.Pin_3, S10.Pin_4, S12.Pin_3, S12.Pin_4, J3.vcc
  N4: 부품3.D5_PWM, J3.pulse
  N5: 부품3.D22, S1.Pin_1, S1.Pin_2, R6.Pin_0
  N6: 부품3.D24, S2.Pin_1, S2.Pin_2, R7.Pin_0
  N7: 부품3.D26, S3.Pin_1, S3.Pin_2, R8.Pin_0
  N8: 부품3.D28, S4.Pin_1, S4.Pin_2, R9.Pin_0
  N9: 부품3.D30, S5.Pin_1, S5.Pin_2, R10.Pin_0
  N10: 부품3.D32, S6.Pin_1, S6.Pin_2, R11.Pin_0
  N11: 부품3.D34, S7.Pin_1, S7.Pin_2, R12.Pin_0
  N12: 부품3.D36, S8.Pin_1, S8.Pin_2, R13.Pin_0
  N13: 부품3.D38, S9.Pin_1, S9.Pin_2, R14.Pin_0
  N14: 부품3.D40, S10.Pin_1, S10.Pin_2, R15.Pin_0
  N15: 부품3.D42, S12.Pin_1, S12.Pin_2, R17.Pin_0

notes:
  namyoon
