# Fritzing sketch taehee-roughsketch (saved by Fritzing 0.9.3b)
breadboards: 1

parts:
  부품1 = Arduino Uno (Rev3) - ICSP
  SP1 = SPEAKER [package=pcb_mount_speaker]
  LED1 = smd LED [color="Red (633nm)" package="0603 [SMD]"]
  LED2 = smd LED [color="Red (633nm)" package="0603 [SMD]"]
  LED3 = smd LED [color="Red (633nm)" package="0603 [SMD]"]
  LED4 = smd LED [color="Red (633nm)" package="0603 [SMD]"]
  LED5 = smd LED [color="Red (633nm)" package="0603 [SMD]"]
  LED6 = smd LED [color="Red (633nm)" package="0603 [SMD]"]
  R1 = Resistor [tolerance=±5% resistance=220 package=THT]
  R2 = Resistor [tolerance=±5% resistance=220 package=THT]
  R3 = Resistor [tolerance=±5% resistance=220 package=THT]

nets:
  N1: 부품1.D8, R1.Pin_1
  N2: 부품1.D9_PWM, R2.Pin_1
  N3: 부품1.D10_PWM/SS, R3.Pin_1
  N4: 부품1.D3_PWM, SP1.-
  N5: 부품1.GND, SP1.+, LED1.cathode, LED2.cathode, LED3.cathode, LED4.cathode, LED5.cathode, LED6.cathode
  N6: LED1.anode, LED2.anode, R1.Pin_0
  N7: LED3.anode, LED4.anode, R2.Pin_0
  N8: LED5.anode, LED6.anode, R3.Pin_0
