# Fritzing sketch youhyun-roughsketch (saved by Fritzing 0.9.3b)
breadboards: 1

parts:
  부품2 = Arduino Uno (Rev3) - ICSP
  DFRobot_DFPlayer_Mini2 = DFRobot DFPlayer Mini [part_number=DFR0299]
  SP2 = SPEAKER [package=pcb_mount_speaker]
  S3 = Pushbutton [package="[SMD]"]
  S4 = Momentary Switch [package=ksa_sealed_tac_switch]
  LED1 = RGB LED (com. cathode, rgb) [package="5 mm [THT]"]
  R1 = Resistor [tolerance=±5% resistance=220 package=THT]
  R2 = Resistor [tolerance=±5% resistance=220 package=THT]
  R3 = Resistor [tolerance=±5% resistance=220 package=THT]
  R4 = Rotary Potentiometer (Small) [maximum_resistance=100kΩ package=THT]
  M6 = DC Motor
  Q3 = NPN-Transistor [package="TO92 [THT]"]
  D3 = Zener Diode [part_number=1N4732A breakdown_voltage=3.6V package="Melf DO-213 AB [SMD]"]
  R5 = Resistor [tolerance=±5% resistance=220 package=THT]

nets:
  N1: 부품2.D8, R1.Pin_0
  N2: 부품2.D9_PWM, R2.Pin_0
  N3: 부품2.D10_PWM/SS, R3.Pin_0
  N4: 부품2.D6_PWM, R5.Pin_0
  3V3: 부품2.3V3, DFRobot_DFPlayer_Mini2.VCC, DFRobot_DFPlayer_Mini2.IO_1, S3.Pin_3, S3.Pin_4, S4.4
  N5: 부품2.5V, M6.pin_1, D3.cathode
  N6: 부품2.GND, DFRobot_DFPlayer_Mini2.GND-1, DFRobot_DFPlayer_Mini2.GND-2, SP2.+, LED1.common_cathode, Q3.E
  N7: DFRobot_DFPlayer_Mini2.SPK_1, DFRobot_DFPlayer_Mini2.SPK_2, R4.wiper
  N8: DFRobot_DFPlayer_Mini2.IO_2, S4.3
  N9: SP2.-, R4.leg1
  N10: S3.Pin_1, S3.Pin_2
  N11: LED1.red_anode, R3.Pin_1
  N12: LED1.green_anode, R2.Pin_1
  N13: LED1.blue_anode, R1.Pin_1
  N14: M6.pin_2, Q3.C, D3.anode
  N15: Q3.B, R5.Pin_1

notes:
  Short press to play previous, long press to decrease volume
  Short press to play next, long press to increase volume
