# Fritzing sketch youhyun-sketch (saved by Fritzing 0.9.3b)
breadboards: 1

parts:
  부품2 = Arduino Uno (Rev3) - ICSP
  DFRobot_DFPlayer_Mini2 = DFRobot DFPlayer Mini [part_number=DFR0299]
  SP2 = SPEAKER [package=pcb_mount_speaker]
  S3 = Pushbutton [package="[SMD]"]
  S4 = Momentary Switch [package=ksa_sealed_tac_switch]
  LED1 = RGB LED (com. cathode, rgb) [package="5 mm [THT]"]
  R1 = Resistor [tolerance=±5% resistance=10k package=THT]
  R3 = Resistor [tolerance=±5% resistance=10k package=THT]  # not connected
  R4 = Rotary Potentiometer (Small) [maximum_resistance=100kΩ package=THT]
  S5 = H-Bridge with L298N
  R5 = Resistor [tolerance=±5% resistance=10k package=THT]
  R6 = Resistor [tolerance=±5% resistance=10k package=THT]
  M1 = DC Motor
  M2 = DC Motor

nets:
  N1: 부품2.D8, S5.IN4
  N2: 부품2.D9_PWM, S5.IN3
  N3: 부품2.D10_PWM/SS, S5.IN2
  N4: 부품2.D11_PWM/MOSI, S5.IN1
  N5: 부품2.D2, R1.Pin_1
  N6: 부품2.D5_PWM, R5.Pin_1
  N7: 부품2.D6_PWM, R6.Pin_1
  3V3: 부품2.3V3, DFRobot_DFPlayer_Mini2.VCC, DFRobot_DFPlayer_Mini2.IO_1, S3.Pin_3, S3.Pin_4, S4.4
  5V: 부품2.5V, S5.5V
  GND: 부품2.GND, DFRobot_DFPlayer_Mini2.GND-1, DFRobot_DFPlayer_Mini2.GND-2, SP2.+, LED1.green_anode, S5.GND
  N8: DFRobot_DFPlayer_Mini2.SPK_1, DFRobot_DFPlayer_Mini2.SPK_2, R4.wiper
  N9: DFRobot_DFPlayer_Mini2.IO_2, S4.3
  N10: SP2.-, R4.leg1
  N11: S3.Pin_1, S3.Pin_2
  N12: LED1.red_anode, R6.Pin_0
  N13: LED1.common_cathode, R5.Pin_0
  N14: LED1.blue_anode, R1.Pin_0
  N15: S5.M1-01, M2.pin_2
  N16: S5.M1-02, M2.pin_1
  N17: S5.M2-01, M1.pin_1
  N18: S5.M2-02, M1.pin_2

notes:
  Short press to play previous, long press to decrease volume
  Short press to play next, long press to increase volume

custom parts:
  H-Bridge with L298N: h-bridge
